// Logisim project Ctl_Shift_Add_Sub_Mov.circ as structural Verilog: 1 circuit, main circuit Shift_Add_Sub_Mov
module Shift_Add_Sub_Mov (
  input  Enable,
  input  [15:0] Instruction,
  output [3:0] Flags_Update_Mask,
  output Carry,
  output Imm32_Enable,
  output [2:0] Rm,
  output [2:0] Rn,
  output [2:0] Rd,
  output [4:0] Imm5,
  output [31:0] Imm32,
  output [3:0] ALU_Opcode
);

  wire bit13, undriven;
  wire [31:0] bit_extender_1_out, bit_extender_2_out;

  // AND_Gate and_1 has open pins: in0=Enable, in1=undriven, out=open
  Bit_Extender #(.in_width(3), .out_width(32)) bit_extender_1 (.out(bit_extender_1_out));  // open: in
  Bit_Extender #(.out_width(32)) bit_extender_2 (.out(bit_extender_2_out));  // open: in
  Multiplexer #(.width(32)) multiplexer_1 (
    .in0(bit_extender_1_out), .in1(bit_extender_2_out), .out(Imm32), .sel(bit13));

  assign ALU_Opcode = {Instruction[15:13], Instruction[13]};
  assign Instruction[12] = Instruction[13];
  assign Rd = Instruction[2:0];

  // Notes on the sheet:
  //   Pull output low on Enable = 0
  //   only ADD and SUB use Rm
  //   Enable carry for SUB since it is reversed in ALU
  //   ALU will use Imm32 instead of Rm
  //   Note: ALU uses Rn register for shifts. Use Rn instead of Rm for shifts (immediate) here too
  //   Note 2: MOV uses RSB ALU opcode with Imm8 reversed so that it is copied to output register
  //   Note 3: Imm32_Enable forces the use of the immediate for Rm register
endmodule
